# Fritzing sketch ArduinoWatch (saved by Fritzing 0.8.7b)
circuit board: 8.46667cm x 5.64444cm
breadboards: 1

parts:
  Part1 = Arduino Pro Mini v13
  RF1 = nRF8001 Bluetooth LE Breakout
  OLED1 = 128x64 Monochrom OLED Display with SPI Control
  CHARGER1 = USB_LiIon_LiPoly_Charger_v1.2
  U1 = Vibration Motor- ROB-08449 [package=vibe-motor-10mm]

nets (from the breadboard view):
  N1: Part1.DTR, Part1.D0/TX
  VIN: Part1.VCC, RF1.VIN, OLED1.Vin, CHARGER1.load_plus_2
  GND: Part1.GND, RF1.GND, OLED1.GND, CHARGER1.load_minus_2, U1.+
  N2: Part1.A1, CHARGER1.stat2
  N3: Part1.A0, CHARGER1.stat1
  N4: Part1.D13/SCK, RF1.SCK, OLED1.Clock
  N5: Part1.D12/MISO, RF1.MISO
  N6: Part1.D11_PWM/MOSI, RF1.MOSI, OLED1.Data
  N7: Part1.D9_PWM, RF1.RST
  N8: Part1.D8, OLED1.Reset
  N9: Part1.D7, OLED1.CS
  N10: Part1.D6_PWM, OLED1.SA0/DC
  N11: Part1.D5_PWM, RF1.REQ
  N12: Part1.D4, U1.-
  N13: Part1.D2, RF1.RDY

custom parts:
  nRF8001 Bluetooth LE Breakout: nRF8001 Breakout Board
